// Logisim project imm_gen.circ as structural Verilog: 4 circuits, main circuit imm_gen
module imm_gen (
  input  [31:0] inst,
  input  [2:0] ImmSel,
  output [31:0] imm
);

  wire [31:0] iformatimm_1_imm;

  IformatImm iformatimm_1 (.imm(iformatimm_1_imm), .inst(inst));
  Multiplexer #(.enable("false"), .select(3), .width(32)) multiplexer_1 (
    .in0(iformatimm_1_imm), .sel(ImmSel));  // open: in1, in2, in3, in4, in5, in6, in7, out

  // Notes on the sheet:
  //   INPUTS to your circuit
  //   DON'T CHANGE THE LOCATIONS OF THE INPUTS AND OUTPUTS!
  //   OUTPUT from your circuit
endmodule

module IformatImm (
  input  [31:0] inst,
  output [31:0] imm
);

  assign imm = {{20{inst[31]}}, inst[31:20]};  // Bit_Extender bit_extender_1
endmodule

module SformatImm (
  input  [31:0] inst,
  output [31:0] imm
);

  assign imm = {{20{inst[31]}}, {inst[31:25], inst[11:7]}};  // Bit_Extender bit_extender_1
endmodule

module IStypeImmGen (
  input  [31:0] inst,
  input  ISsel,
  output [31:0] imm
);

  wire [4:0] multiplexer_1_out;

  Multiplexer #(.enable("false"), .width(5)) multiplexer_1 (
    .in0(inst[11:7]), .in1(inst[24:20]), .out(multiplexer_1_out), .sel(ISsel));
  assign imm = {{20{inst[31]}}, {inst[31:25], multiplexer_1_out}};  // Bit_Extender bit_extender_1
endmodule
